# Fritzing sketch Btr-Btn (saved by Fritzing 1.0.2b)

parts:
  S1 = Taiway 100-SP-X-T1 SPDT Miniature Toggle Switch [part_number=100-SP-X-T1-0-0-B1-M2 package=THT]
  battery1 = Battery3AA-A [part_number=001 package=Pack-tve]
  battery2 = Battery3AA-A [part_number=001 package=Pack-tve]
  M1 = gear-motor
  M2 = gear-motor
  S2 = Square Pushbutton

nets:
  N1: S1.COM, battery1.-, battery2.-
  N2: S1.L1, M1.pin_1
  N3: S1.L2, M2.pin_2, S2.leg1
  N4: battery1.+, M1.pin_2, S2.leg0
  N5: battery2.+, M2.pin_1

custom parts:
  Battery3AA-A: Блок 3 элементов питания AAA по 1.5В
