# Fritzing sketch Dva-v-odnom_v9 (saved by Fritzing 1.0.2b)

parts:
  Master-KRUTJAK = Arduino Pro Mini v13
  Slave-KRUTJAK = Arduino Pro Mini v13
  Драйвер_мотора = IFR520 MOS module [package=THT]
  btrSlave = Battery3AAA [part_number=001 package=Pack-tve]
  btrMaster = Battery3AAA [part_number=001 package=Pack-tve]
  ИКД = fc-51 [package=THT]
  M1 = gear-motor
  SG3 = Buzzer 12mm [package=buzzer-ccv]
  LED1 = LEDs [package=led10mm]
  OLED_I2C1 = OLED 128x64 I2C Monochrome Display
  SG4 = Buzzer 12mm [package=buzzer-ccv]
  On-Off = Square Pushbutton
  R1 = Resistor [tolerance=±5% power=0.25W resistance=470 package=THT]
  Sp1 = Spaika
  Sp2 = Spaika
  Sp3 = Spaika
  Sp4 = Spaika
  Sp5 = Spaika
  Sp6 = Spaika
  Sp7 = Spaika
  S1 = Taiway 100-SP-X-T1 SPDT Miniature Toggle Switch [part_number=100-SP-X-T1-0-0-B1-M2 package=THT]

nets:
  GND: Master-KRUTJAK.GND, Slave-KRUTJAK.GND, Драйвер_мотора.GND, btrMaster.-, ИКД.pin2, M1.pin_1, SG3.2, OLED_I2C1.GND
  N1: Master-KRUTJAK.A4, Sp2.leg1
  N2: Master-KRUTJAK.A5, Sp3.leg1
  VCC: Master-KRUTJAK.VCC, ИКД.pin3, OLED_I2C1.VDD
  N3: Master-KRUTJAK.D6_PWM, Slave-KRUTJAK.D4
  N4: Master-KRUTJAK.D5_PWM, Slave-KRUTJAK.D3_PWM
  N5: Master-KRUTJAK.D3_PWM, SG3.1
  N6: Master-KRUTJAK.D2, Sp1.leg0
  VCC_2: Slave-KRUTJAK.VCC, Драйвер_мотора.VCC
  N7: Slave-KRUTJAK.D7, Sp7.leg1
  N8: Slave-KRUTJAK.D6_PWM, Драйвер_мотора.V-
  N9: Драйвер_мотора.SIG, Sp7.leg0
  N10: Драйвер_мотора.VIN, M1.pin_2
  N11: btrSlave.-, LED1.C, SG4.2
  N12: btrSlave.+, Sp4.leg0
  N13: btrMaster.+, S1.COM
  N14: ИКД.pin1, Sp1.leg1
  N15: LED1.A, R1.Pin_0
  N16: OLED_I2C1.SDA, Sp2.leg0
  N17: OLED_I2C1.SCK, Sp3.leg0
  N18: SG4.1, Sp6.leg1
  N19: On-Off.leg0, Sp5.leg0, Sp6.leg0
  N20: On-Off.leg1, Sp4.leg1
  N21: R1.Pin_1, Sp5.leg1

custom parts:
  Battery3AAA: Блок 3 элементов питания AAA по 1.5В
  Spaika: Spaika - соединение 2 проводов разного цвета
