# Fritzing sketch MainProjector_v5 (saved by Fritzing 1.0.2b)

parts:
  S1 = Taiway 100-SP-X-T1 SPDT Miniature Toggle Switch [part_number=100-SP-X-T1-0-0-B1-M2 package=THT]
  Master-KRUTJAK = Arduino Pro Mini v13
  Slave-KRUTJAK = Arduino Pro Mini v13
  Драйвер_мотора = IFR520 MOS module [package=THT]
  S2 = Square Pushbutton
  btrSlave = Battery3AAA [part_number=001 package=Pack-tve]
  btrMaster = Battery3AAA [part_number=001 package=Pack-tve]
  ИКД = fc-51 [package=THT]
  M1 = gear-motor
  SG3 = Buzzer 12mm [package=buzzer-ccv]
  LED1 = LEDs [package=led10mm]
  OLED_I2C1 = OLED 128x64 I2C Monochrome Display
  SG4 = Buzzer 12mm [package=buzzer-ccv]

nets:
  GND: S1.COM, Master-KRUTJAK.GND, Slave-KRUTJAK.GND, Драйвер_мотора.GND, btrSlave.-, btrMaster.-, ИКД.pin2, M1.pin_1, SG3.2, LED1.C, OLED_I2C1.GND, SG4.2
  VCC: S1.L1, S1.L2, Master-KRUTJAK.VCC, Slave-KRUTJAK.VCC, Драйвер_мотора.VCC, S2.leg1, btrSlave.+, btrMaster.+, ИКД.pin3, LED1.A, OLED_I2C1.VDD, SG4.1
  N1: Master-KRUTJAK.A4, OLED_I2C1.SDA
  N2: Master-KRUTJAK.A5, OLED_I2C1.SCK
  N3: Master-KRUTJAK.D6_PWM, Slave-KRUTJAK.D4
  N4: Master-KRUTJAK.D5_PWM, Slave-KRUTJAK.D3_PWM
  N5: Master-KRUTJAK.D3_PWM, SG3.1
  N6: Master-KRUTJAK.D2, ИКД.pin1
  N7: Slave-KRUTJAK.D7, Драйвер_мотора.SIG
  N8: Slave-KRUTJAK.D6_PWM, Драйвер_мотора.V-
  N9: Драйвер_мотора.VIN, S2.leg0, M1.pin_2

custom parts:
  Battery3AAA: Блок 3 элементов питания AAA по 1.5В
