# Fritzing sketch MainSwitch12 (saved by Fritzing 1.0.2b)

parts:
  btrMaster = Battery3AA-A [part_number=001 package=Pack-tve]
  btrSlave = Battery3AA-A [part_number=001 package=Pack-tve]
  S1 = Taiway 100-SP-X-T1 SPDT Miniature Toggle Switch [part_number=100-SP-X-T1-0-0-B1-M2 package=THT]
  Master-KRUTJAK = Arduino Pro Mini v13
  Slave-KRUTJAK = Arduino Pro Mini v13

nets:
  VCC: btrMaster.+, btrSlave.+, Master-KRUTJAK.VCC, Slave-KRUTJAK.VCC
  N1: btrMaster.-, S1.L2
  N2: btrSlave.-, S1.L1
  GND: S1.COM, Master-KRUTJAK.GND, Slave-KRUTJAK.GND

custom parts:
  Battery3AA-A: Блок 3 элементов питания AAA по 1.5В
