# Fritzing sketch MainSwitch1g2v (saved by Fritzing 1.0.2b)

parts:
  S1 = Taiway 100-SP-X-T1 SPDT Miniature Toggle Switch [part_number=100-SP-X-T1-0-0-B1-M2 package=THT]
  Master-KRUTJAK = Arduino Pro Mini v13
  Slave-KRUTJAK = Arduino Pro Mini v13
  Motor = gear-motor
  Драйвер_мотора = IFR520 MOS module [package=THT]  # not connected
  S2 = Square Pushbutton
  btrSlave = Battery3AAA [part_number=001 package=Pack-tve]
  btrMaster = Battery3AAA [part_number=001 package=Pack-tve]

nets:
  VCC: S1.COM, Master-KRUTJAK.VCC, Slave-KRUTJAK.VCC, btrSlave.+, btrMaster.+
  N1: S1.L1, Motor.pin_1
  N2: S1.L2, Slave-KRUTJAK.GND
  N3: Master-KRUTJAK.GND, btrMaster.-
  N4: Motor.pin_2, S2.leg1
  N5: S2.leg0, btrSlave.-

custom parts:
  Battery3AAA: Блок 3 элементов питания AAA по 1.5В
