# Fritzing sketch MainSwitch_v1 (saved by Fritzing 1.0.2b)

parts:
  S1 = Taiway 100-SP-X-T1 SPDT Miniature Toggle Switch [part_number=100-SP-X-T1-0-0-B1-M2 package=THT]
  Master-KRUTJAK = Arduino Pro Mini v13
  Slave-KRUTJAK = Arduino Pro Mini v13
  Motor = gear-motor
  Драйвер_мотора = IFR520 MOS module [package=THT]
  S2 = Square Pushbutton
  btrSlave = Battery3AAA [part_number=001 package=Pack-tve]
  btrMaster = Battery3AAA [part_number=001 package=Pack-tve]
  ИКД = fc-51 [package=THT]  # not connected

nets:
  GND: S1.COM, Master-KRUTJAK.GND, Slave-KRUTJAK.GND, Драйвер_мотора.GND, btrSlave.-, btrMaster.-
  N1: S1.L1, S2.leg1
  VCC: S1.L2, Master-KRUTJAK.VCC, Slave-KRUTJAK.VCC
  N2: Motor.pin_1, btrSlave.+
  N3: Motor.pin_2, S2.leg0
  N4: Драйвер_мотора.VIN, btrMaster.+

custom parts:
  Battery3AAA: Блок 3 элементов питания AAA по 1.5В
