# Fritzing sketch MainSwitch_v2 (saved by Fritzing 1.0.2b)

parts:
  S1 = Taiway 100-SP-X-T1 SPDT Miniature Toggle Switch [part_number=100-SP-X-T1-0-0-B1-M2 package=THT]
  Master-KRUTJAK = Arduino Pro Mini v13
  Slave-KRUTJAK = Arduino Pro Mini v13
  Драйвер_мотора = IFR520 MOS module [package=THT]  # not connected
  S2 = Square Pushbutton  # not connected
  btrSlave = Battery3AAA [part_number=001 package=Pack-tve]
  btrMaster = Battery3AAA [part_number=001 package=Pack-tve]
  ИКД = fc-51 [package=THT]
  M1 = gear-motor  # not connected

nets:
  N1: S1.COM, Slave-KRUTJAK.GND, btrSlave.-, btrMaster.-, ИКД.pin2
  VCC: S1.L2, Master-KRUTJAK.VCC, Slave-KRUTJAK.VCC, btrMaster.+, ИКД.pin3

custom parts:
  Battery3AAA: Блок 3 элементов питания AAA по 1.5В
