# Fritzing sketch MainSwitch_v3 (saved by Fritzing 1.0.2b)

parts:
  S1 = Taiway 100-SP-X-T1 SPDT Miniature Toggle Switch [part_number=100-SP-X-T1-0-0-B1-M2 package=THT]
  Master-KRUTJAK = Arduino Pro Mini v13
  Slave-KRUTJAK = Arduino Pro Mini v13
  Драйвер_мотора = IFR520 MOS module [package=THT]
  S2 = Square Pushbutton
  btrSlave = Battery3AAA [part_number=001 package=Pack-tve]
  btrMaster = Battery3AAA [part_number=001 package=Pack-tve]
  ИКД = fc-51 [package=THT]
  M1 = gear-motor

nets:
  GND: S1.COM, Slave-KRUTJAK.GND, Драйвер_мотора.GND, btrSlave.-, btrMaster.-, ИКД.pin2, M1.pin_1
  VCC: S1.L2, Master-KRUTJAK.VCC, Slave-KRUTJAK.VCC, btrMaster.+, ИКД.pin3
  N1: Драйвер_мотора.VCC, S2.leg1, btrSlave.+
  N2: Драйвер_мотора.VIN, S2.leg0, M1.pin_2

custom parts:
  Battery3AAA: Блок 3 элементов питания AAA по 1.5В
