# Fritzing sketch upravlyaem-skorostyu-ehlektromotora (saved by Fritzing 1.0.2b)
circuit board: 8.46667cm x 5.64444cm
breadboards: 1

parts:
  IRFZ24N_n-channel_Transistor1 = IRFZ24N n-channel
  R1 = Rotary Potentiometer (Small) [maximum_resistance=10kΩ knob_status=50% power=0.5W package=THT]
  Компонент1 = Arduino Uno (Rev3)
  battery1 = Battery3AA-A [part_number=001 package=Pack-tve]
  R2 = Resistor [tolerance=±5% power=0.5W resistance=10k package=THT]
  M1 = gear-motor

nets:
  N1: IRFZ24N_n-channel_Transistor1.gate_-_затвор, Компонент1.D10_PWM/SS, R2.Pin_1
  N2: IRFZ24N_n-channel_Transistor1.drain_-_сток, M1.pin_1
  N3: IRFZ24N_n-channel_Transistor1.source_-_исток, R1.leg2, Компонент1.GND, battery1.-, R2.Pin_0
  N4: R1.leg1, Компонент1.5V
  N5: R1.wiper, Компонент1.A0
  N6: battery1.+, M1.pin_2

notes:
  upravlyaem-skorostyu-ehlektromotora
  ************************************************************

custom parts:
  IRFZ24N n-channel: A MOSFET N-Channel Transistor. Максимальное напряжение сток-исток (Uси): 55В; Максимальный продолжительный ток стока (Iс): 17А; Максимальный импульсный ток стока (Iс): 68А; Ток утечки стока: 25мкА (при Uси = 55В); Ток утечки затвора: 100нА (при Uзи = 20В); Сопротивление открытого канала (Rси): 70мOм (0.07Ом); Пороговое напряжение затвор-исток (UGS): 2... 4В; Максимальное напряжение затвор-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
  Battery3AA-A: Блок 3 элементов питания AAA по 1.5В
