# Fritzing sketch I2c_Scanner (saved by Fritzing 1.0.2b)
breadboards: 1

parts:
  Компонент1 = LCD1602-I2C
  Компонент2 = Arduino Pro Mini v13

nets:
  N1: Компонент1.SDA, Компонент2.A4
  N2: Компонент1.SCL, Компонент2.A5

custom parts:
  LCD1602-I2C: A standard character display, usually with 2x16 characters. Comes in many colors with LCM1602 IIC attached.
