# Fritzing sketch kvizzy1-esp32-cam (saved by Fritzing 1.0.2b)
breadboards: 1

parts:
  USB_UART1 = USB-TTL UART
  ESP32-CAM1 = ESP32-CAM_tve
  Компонент1 = Arduino Pro Mini (5V)
  R1 = Resistor [tolerance=±5% power=0.25W resistance=10k package=THT]
  R2 = Resistor [tolerance=±5% power=0.25W resistance=22k package=THT]

nets:
  N1: USB_UART1.pin6, ESP32-CAM1.GND#7, Компонент1.GND
  5V: USB_UART1.pin7, ESP32-CAM1.5V, Компонент1.VCC
  N2: USB_UART1.pin8, ESP32-CAM1.GPIO3_/_RX
  N3: USB_UART1.pin9, ESP32-CAM1.GPIO1_/_TX
  N4: ESP32-CAM1.GPIO16, R1.Pin_0, R2.Pin_0
  N5: ESP32-CAM1.GPIO0, Компонент1.D4
  N6: ESP32-CAM1.GND#16, R2.Pin_1
  N7: Компонент1.D3, R1.Pin_1

notes:
  esp32-cam IO0: TX => RX:D4 Pro Mini - просто провод
  esp32-cam IO16:RX => TX:D3 Pro Mini - делитель напряжения

custom parts:
  USB-TTL UART: USB programmer interface incorporating Silicon Labs CP2102 UART
  ESP32-CAM_tve: The ESP32-CAM has a very competitive small-size camera module that can operate independently as a minimum system with a footprint of only 27*40.5*4.5mm and a deep sleep current of up to 6mA.
