# Fritzing sketch kvizzy1-pervushechka (saved by Fritzing 1.0.2b)
breadboards: 1

parts:
  Компонент1 = LCD1602-I2C
  Компонент2 = Arduino Pro Mini v13
  BAT1 = Battery Holders [package=battery-aa-panel]
  J1 = Piezo Speaker
  J2 = HC-SR501 [form="♀ (female)" package=THT]

nets:
  GND: Компонент1.GND, Компонент2.GND, BAT1.-, J1.pin1, J2.GND
  VCC: Компонент1.VCC, Компонент2.VCC, BAT1.+, J2.VCC
  N1: Компонент1.SDA, Компонент2.A4
  N2: Компонент1.SCL, Компонент2.A5
  N3: Компонент2.D12/MISO, J1.pin2
  N4: Компонент2.D2, J2.SIG

custom parts:
  LCD1602-I2C: A standard character display, usually with 2x16 characters. Comes in many colors with LCM1602 IIC attached.
