# Fritzing sketch LedyEs (saved by Fritzing 1.0.2b)
breadboards: 1

parts:
  Компонент1 = Arduino Uno (Rev3) - ICSP
  PowerUnit12V1 = PowerUnit12V [package=bc12vpc]
  IRFZ24N_Transistor1 = IRFZ24N n-channel
  IRFZ24N_Transistor2 = IRFZ24N n-channel
  IRFZ24N_Transistor3 = IRFZ24N n-channel
  R1 = Resistor [tolerance=±5% power=0.25W resistance=10k package=THT]
  R2 = Resistor [tolerance=±5% power=0.25W resistance=10k package=THT]
  R3 = Resistor [tolerance=±5% power=0.25W resistance=10k package=THT]
  R4 = Resistor [tolerance=±5% power=0.25W resistance=100 package=THT]
  R5 = Resistor [tolerance=±5% power=0.25W resistance=100 package=THT]
  R6 = Resistor [tolerance=±5% power=0.25W resistance=100 package=THT]
  RGB_Strip_LED1 = RGB Strip LED

nets:
  N1: Компонент1.D3_PWM, R4.Pin_1
  N2: Компонент1.D5_PWM, R5.Pin_1
  N3: Компонент1.D7, R6.Pin_1
  N4: PowerUnit12V1.V+, RGB_Strip_LED1.Common_Connect#4
  N5: PowerUnit12V1.V-, IRFZ24N_Transistor1.source_-_исток, IRFZ24N_Transistor2.source_-_исток, IRFZ24N_Transistor3.source_-_исток, R1.Pin_1, R2.Pin_1, R3.Pin_1
  N6: IRFZ24N_Transistor1.gate_-_затвор, R1.Pin_0, R4.Pin_0
  N7: IRFZ24N_Transistor1.drain_-_сток, RGB_Strip_LED1.Green_Connect
  N8: IRFZ24N_Transistor2.gate_-_затвор, R2.Pin_0, R5.Pin_0
  N9: IRFZ24N_Transistor2.drain_-_сток, RGB_Strip_LED1.Red_Connect#6
  N10: IRFZ24N_Transistor3.gate_-_затвор, R3.Pin_0, R6.Pin_0
  N11: IRFZ24N_Transistor3.drain_-_сток, RGB_Strip_LED1.Blue_Connect

custom parts:
  PowerUnit12V: 12V board-mount battery cradle
  IRFZ24N n-channel: A MOSFET N-Channel Transistor. Максимальное напряжение сток-исток (Uси): 55В; Максимальный продолжительный ток стока (Iс): 17А; Максимальный импульсный ток стока (Iс): 68А; Ток утечки стока: 25мкА (при Uси = 55В); Ток утечки затвора: 100нА (при Uзи = 20В); Сопротивление открытого канала (Rси): 70мOм (0.07Ом); Пороговое напряжение затвор-исток (UGS): 2... 4В; Максимальное напряжение затвор-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
  RGB Strip LED: A tri-color Strip LED with red, green and blue. Pin order: red - common cathode - blue - green
